// Digital circuit mainBus.dig as structural Verilog
module mainBus (
  input  clk,
  input  ALU_OUTe,
  input  ALU_RSLTe,
  input  ACC_e
);

  wire DAddr_e, NXT_I, or_1_out, PCCNT_e, PCLD_e, PCOUT_e, RInst_E, RRam_e, RST;
  wire [2:0] counter_1_out;
  wire [3:0] PGM_mem_d;
  wire [4:0] Reg_I_p3;
  wire [7:0] _5bitpc2_1_pc_out, Acc_W_q_x, ALU_dsp, PGM_mem_d_2, Reg_I_2_q_x;
  wire [11:0] MicroCodigo_out;

  or or_1 (or_1_out, RST, NXT_I);
  Button RESET (.out(RST));
  Counter #(.Bits(3)) counter_1 (.en(1'b1), .C(clk), .clr(or_1_out), .out(counter_1_out));  // open: ovf
  _5bitPC2 _5bitpc2_1 (
    .PC_in(_5bitpc2_1_pc_out), .Le_a(PCLD_e), .CNTe_a(PCCNT_e), .CLK(clk), .CLR(RST), .Re_a(PCOUT_e),
    .PC_out(_5bitpc2_1_pc_out));
  // sapRegX Reg_I: pin names not known; wires that end beside it: 1'b1, _5bitpc2_1_pc_out, Reg_I_p3, RInst_E
  ROM #(.AddrBits(5), .Bits(12)) PGM_mem (.A(Reg_I_p3), .sel(1'b1), .D({PGM_mem_d_2, PGM_mem_d}));
  assign _5bitpc2_1_pc_out = DAddr_e ? PGM_mem_d_2 : 8'bz;  // Driver driver_1
  LookUpTable #(.Bits(12)) MicroCodigo (
    .in0(counter_1_out[0]), .in1(counter_1_out[1]), .in2(counter_1_out[2]), .in3(PGM_mem_d[0]),
    .in4(PGM_mem_d[1]), .in5(PGM_mem_d[2]), .in6(PGM_mem_d[3]), .out(MicroCodigo_out));
  Seven_Seg_Hex seven_seg_hex_1 (.d(_5bitpc2_1_pc_out[7:4]), .dp(1'b0));
  sapRegX Acc_W (.E_in(ACC_e), .D_x(_5bitpc2_1_pc_out), .E_out(1'b1), .Q_x(Acc_W_q_x));
  sapRegX Reg_I_2 (.E_in(RRam_e), .D_x(_5bitpc2_1_pc_out), .E_out(1'b1), .Q_x(Reg_I_2_q_x));
  Seven_Seg_Hex seven_seg_hex_2 (.d(_5bitpc2_1_pc_out[3:0]), .dp(1'b0));
  // sapALU_1 sapalu_1_1: pin names not known; wires that end beside it: Acc_W_q_x, _5bitpc2_1_pc_out, ALU_dsp
  RAMDualPort #(.AddrBits(8), .Bits(8)) RAM (
    .A(Reg_I_2_q_x), .Din(_5bitpc2_1_pc_out), .C(clk), .D(_5bitpc2_1_pc_out));  // open: str, ld
  sapRegX Reg_B (.E_in(ALU_RSLTe), .D_x(ALU_dsp), .E_out(ALU_OUTe), .Q_x(_5bitpc2_1_pc_out));
  Seven_Seg_Hex seven_seg_hex_3 (.d(ALU_dsp[7:4]), .dp(1'b0));
  Seven_Seg_Hex seven_seg_hex_4 (.d(ALU_dsp[3:0]), .dp(1'b0));

  // Notes on the sheet:
  //   Formato da instrução
  //   OOOOAAAAAAAA
  //   OOOO -> Codigo de instrucao
  //   AAAAAAAA -->> Endereco do operando / valor
  //   256 byte
  //   ScratchPad memory
endmodule
